// Logisim project MatchingGame4x4.circ as structural Verilog: 1 circuit, main circuit main
// 0x3
module main (
);

  wire Acertado00, Acertado01, Acertado02, Acertado03, Acertado10, Acertado11, Acertado12, Acertado13,
       Acertado20, Acertado21, Acertado22, Acertado23, Acertado30, Acertado31, Acertado32, Acertado33,
       and_18_out, and_19_out, and_20_out, and_21_out, and_22_out, and_23_out, and_24_out, and_25_out,
       and_26_out, and_27_out, and_28_out, and_29_out, and_30_out, and_31_out, and_32_out, and_33_out,
       and_34_out, and_35_out, and_36_out, and_37_out, and_38_out, and_39_out, and_40_out, and_41_out,
       and_42_out, and_43_out, and_44_out, and_45_out, and_51_out, and_52_out, and_53_out, and_54_out,
       and_55_out, and_56_out, and_57_out, and_58_out, and_59_out, and_60_out, and_61_out, and_62_out,
       and_63_out, and_64_out, and_65_out, and_66_out, and_67_out, and_68_out, and_69_out, and_70_out,
       and_71_out, and_72_out, and_73_out, and_74_out, and_75_out, and_76_out, and_77_out, and_78_out,
       and_79_out, and_80_out, and_81_out, and_82_out, and_83_out, and_84_out, and_85_out, and_86_out,
       and_87_out, and_88_out, and_89_out, and_90_out, and_91_out, and_92_out, and_93_out, and_94_out,
       and_95_out, and_96_out, and_97_out, and_98_out, and_99_out, and_100_out, and_101_out, and_102_out,
       and_103_out, and_104_out, and_105_out, and_106_out, and_107_out, Bloqueado, Coluna, comparator_1_eq,
       comparator_2_eq, Confirma, Estado_0, Estado_1, Estado_2, Estado_3, Jogador_1, Jogador_2, L00, L01,
       L02, L03, L10, L11, L12, L13, L20, L21, L22, L23, L30, L31, L32, L33, Linha, Mux00, Mux01, Mux02,
       Mux03, Mux10, Mux11, Mux12, Mux13, Mux20, Mux21, Mux22, Mux23, Mux30, Mux31, Mux32, Mux33, or_10_out,
       or_19_out, or_20_out, or_21_out, or_22_out, or_23_out, or_24_out, or_25_out, or_26_out, or_27_out,
       or_28_out, or_29_out, or_30_out, or_31_out, or_32_out, or_33_out, or_34_out, Reset, V1, V2, Verifica;
  wire [1:0] Coluna_N1, Coluna_N2, counter_6_q, Linha_N1, Linha_N2, nColuna, nLinha;
  wire [3:0] multiplexer_1_out, multiplexer_2_out, N00, N01, N02, N03, N10, N11, N12, N13, N20, N21, N22,
       N23, N30, N31, N32, N33, PJ1, PJ2;

  LED led_1 (.in(Jogador_1));
  Hex_Digit_Display hex_digit_display_1 (.value(PJ1));  // open: dp
  and and_1 (L00, ~nLinha[0], ~nLinha[1], ~nColuna[0], ~nColuna[1]);  // AND_Gate
  and and_2 (L01, ~nLinha[0], ~nLinha[1], nColuna[0], ~nColuna[1]);  // AND_Gate
  and and_3 (L02, ~nLinha[0], ~nLinha[1], ~nColuna[0], nColuna[1]);  // AND_Gate
  and and_4 (L03, ~nLinha[0], ~nLinha[1], nColuna[0], nColuna[1]);  // AND_Gate
  and and_5 (L10, nLinha[0], ~nLinha[1], ~nColuna[0], ~nColuna[1]);  // AND_Gate
  and and_6 (L11, nLinha[0], ~nLinha[1], nColuna[0], ~nColuna[1]);  // AND_Gate
  and and_7 (L12, nLinha[0], ~nLinha[1], ~nColuna[0], nColuna[1]);  // AND_Gate
  and and_8 (L13, nLinha[0], ~nLinha[1], nColuna[0], nColuna[1]);  // AND_Gate
  and and_9 (L20, ~nLinha[0], nLinha[1], ~nColuna[0], ~nColuna[1]);  // AND_Gate
  and and_10 (L21, ~nLinha[0], nLinha[1], nColuna[0], ~nColuna[1]);  // AND_Gate
  and and_11 (L22, ~nLinha[0], nLinha[1], ~nColuna[0], nColuna[1]);  // AND_Gate
  and and_12 (L23, ~nLinha[0], nLinha[1], nColuna[0], nColuna[1]);  // AND_Gate
  and and_13 (L30, nLinha[0], nLinha[1], ~nColuna[0], ~nColuna[1]);  // AND_Gate
  and and_14 (L31, nLinha[0], nLinha[1], nColuna[0], ~nColuna[1]);  // AND_Gate
  and and_15 (L32, nLinha[0], nLinha[1], ~nColuna[0], nColuna[1]);  // AND_Gate
  and and_16 (L33, nLinha[0], nLinha[1], nColuna[0], nColuna[1]);
  LED led_2 (.in(L00));
  Hex_Digit_Display hex_digit_display_2 (.value(N00));  // open: dp
  LED led_3 (.in(L10));
  Hex_Digit_Display hex_digit_display_3 (.value(N10));  // open: dp
  LED led_4 (.in(L20));
  Hex_Digit_Display hex_digit_display_4 (.value(N20));  // open: dp
  LED led_5 (.in(L30));
  Hex_Digit_Display hex_digit_display_5 (.value(N30));  // open: dp
  LED led_6 (.in(L01));
  Hex_Digit_Display hex_digit_display_6 (.value(N01));  // open: dp
  LED led_7 (.in(L11));
  Hex_Digit_Display hex_digit_display_7 (.value(N11));  // open: dp
  LED led_8 (.in(L21));
  Hex_Digit_Display hex_digit_display_8 (.value(N21));  // open: dp
  LED led_9 (.in(L31));
  Hex_Digit_Display hex_digit_display_9 (.value(N31));  // open: dp
  Button button_1 (.out(Linha));
  Button button_2 (.out(Confirma));
  LED led_10 (.in(L02));
  Hex_Digit_Display hex_digit_display_10 (.value(N02));  // open: dp
  LED led_11 (.in(L12));
  Hex_Digit_Display hex_digit_display_11 (.value(N12));  // open: dp
  LED led_12 (.in(L22));
  Hex_Digit_Display hex_digit_display_12 (.value(N22));  // open: dp
  LED led_13 (.in(L32));
  Hex_Digit_Display hex_digit_display_13 (.value(N32));  // open: dp
  Button button_3 (.out(Coluna));
  Button button_4 (.out(Reset));
  Multiplexer #(.select(4), .width(4), .enable("false")) multiplexer_1 (
    .in0(N00), .in1(N10), .in2(N20), .in3(N30), .in4(N01), .in5(N11), .in6(N21), .in7(N31), .in8(N02),
    .in9(N12), .in10(N22), .in11(N32), .in12(N03), .in13(N13), .in14(N23), .in15(N33),
    .out(multiplexer_1_out), .sel({Coluna_N1, Linha_N1}));
  Multiplexer #(.select(4), .width(4), .enable("false")) multiplexer_2 (
    .in0(N00), .in1(N10), .in2(N20), .in3(N30), .in4(N01), .in5(N11), .in6(N21), .in7(N31), .in8(N02),
    .in9(N12), .in10(N22), .in11(N32), .in12(N03), .in13(N13), .in14(N23), .in15(N33),
    .out(multiplexer_2_out), .sel({Coluna_N2, Linha_N2}));
  LED led_14 (.in(L03));
  Hex_Digit_Display hex_digit_display_14 (.value(N03));  // open: dp
  LED led_15 (.in(L13));
  Hex_Digit_Display hex_digit_display_15 (.value(N13));  // open: dp
  LED led_16 (.in(L23));
  Hex_Digit_Display hex_digit_display_16 (.value(N23));  // open: dp
  LED led_17 (.in(L33));
  Hex_Digit_Display hex_digit_display_17 (.value(N33));  // open: dp
  or or_1 (Bloqueado, V1, V2);
  Comparator #(.width(4)) comparator_1 (
    .a(multiplexer_1_out), .b(multiplexer_2_out), .eq(comparator_1_eq));  // open: gt, lt
  LED led_18 (.in(Jogador_2));
  Hex_Digit_Display hex_digit_display_18 (.value(PJ2));  // open: dp
  Multiplexer #(.width(4), .enable("false")) multiplexer_3 (.in1(4'b0000), .out(N00), .sel(Mux00));  // open: in0
  Multiplexer #(.width(4), .enable("false")) multiplexer_4 (.in1(4'b0001), .out(N10), .sel(Mux10));  // open: in0
  Multiplexer #(.width(4), .enable("false")) multiplexer_5 (.in1(4'b0010), .out(N20), .sel(Mux20));  // open: in0
  Multiplexer #(.width(4), .enable("false")) multiplexer_6 (.in1(4'b0011), .out(N30), .sel(Mux30));  // open: in0
  and and_17 (Verifica, comparator_1_eq, Estado_3);
  and and_18 (and_18_out, ~Linha_N1[0], ~Linha_N1[1], ~Coluna_N1[0], ~Coluna_N1[1], ~Estado_0);  // AND_Gate
  and and_19 (and_19_out, ~Linha_N2[0], ~Linha_N2[1], ~Coluna_N2[0], ~Coluna_N2[1], Estado_2);  // AND_Gate
  and and_20 (and_20_out, Linha_N1[0], ~Linha_N1[1], ~Coluna_N1[0], ~Coluna_N1[1], ~Estado_0);  // AND_Gate
  and and_21 (and_21_out, Linha_N2[0], ~Linha_N2[1], ~Coluna_N2[0], ~Coluna_N2[1], Estado_2);  // AND_Gate
  and and_22 (and_22_out, ~Linha_N1[0], Linha_N1[1], ~Coluna_N1[0], ~Coluna_N1[1], ~Estado_0);  // AND_Gate
  and and_23 (and_23_out, ~Linha_N2[0], Linha_N2[1], ~Coluna_N2[0], ~Coluna_N2[1], Estado_2);  // AND_Gate
  and and_24 (and_24_out, Linha_N1[0], Linha_N1[1], ~Coluna_N1[0], ~Coluna_N1[1], ~Estado_0);  // AND_Gate
  and and_25 (and_25_out, Linha_N2[0], Linha_N2[1], ~Coluna_N2[0], ~Coluna_N2[1], Estado_2);  // AND_Gate
  Multiplexer #(.width(4), .enable("false")) multiplexer_7 (.in1(4'b0001), .out(N01), .sel(Mux01));  // open: in0
  Multiplexer #(.width(4), .enable("false")) multiplexer_8 (.in1(4'b0000), .out(N11), .sel(Mux11));  // open: in0
  Multiplexer #(.width(4), .enable("false")) multiplexer_9 (.in1(4'b0011), .out(N21), .sel(Mux21));  // open: in0
  Multiplexer #(.width(4), .enable("false")) multiplexer_10 (.in1(4'b0010), .out(N31), .sel(Mux31));  // open: in0
  or or_2 (Mux00, and_18_out, Acertado00, and_19_out);
  or or_3 (Mux10, and_20_out, Acertado10, and_21_out);
  or or_4 (Mux20, and_22_out, Acertado20, and_23_out);
  or or_5 (Mux30, and_24_out, Acertado30, and_25_out);
  Counter #(.width(4), .max('hf)) counter_1 (.Q(PJ1), .clk(and_26_out), .clr(Reset));  // open: load, D, count, carry
  and and_26 (and_26_out, Jogador_1, Verifica);
  Counter #(.width(4), .max('hf)) counter_2 (.Q(PJ2), .clk(and_27_out), .clr(Reset));  // open: load, D, count, carry
  and and_27 (and_27_out, Verifica, Jogador_2);
  Multiplexer #(.width(4), .enable("false")) multiplexer_11 (.in1(4'b0100), .out(N02), .sel(Mux02));  // open: in0
  Multiplexer #(.width(4), .enable("false")) multiplexer_12 (.in1(4'b0101), .out(N12), .sel(Mux12));  // open: in0
  Multiplexer #(.width(4), .enable("false")) multiplexer_13 (.in1(4'b0110), .out(N22), .sel(Mux22));  // open: in0
  Multiplexer #(.width(4), .enable("false")) multiplexer_14 (.in1(4'b0111), .out(N32), .sel(Mux32));  // open: in0
  Multiplexer #(.width(4), .enable("false")) multiplexer_15 (.in1(4'b0101), .out(N03), .sel(Mux03));  // open: in0
  Multiplexer #(.width(4), .enable("false")) multiplexer_16 (.in1(4'b0100), .out(N13), .sel(Mux13));  // open: in0
  Multiplexer #(.width(4), .enable("false")) multiplexer_17 (.in1(4'b0111), .out(N23), .sel(Mux23));  // open: in0
  Multiplexer #(.width(4), .enable("false")) multiplexer_18 (.in1(4'b0110), .out(N33), .sel(Mux33));  // open: in0
  Counter #(.width(1), .max('h1)) counter_3 (
    .Q(Jogador_2), .clk(Estado_0), .clr(Reset));  // open: load, D, count, carry
  Counter #(.width(2), .max('h3)) counter_4 (.Q(nLinha), .clk(Linha), .clr(Reset));  // open: load, D, count, carry
  and and_28 (and_28_out, ~Linha_N1[0], ~Linha_N1[1], Coluna_N1[0], ~Coluna_N1[1], ~Estado_0);  // AND_Gate
  or or_6 (Mux01, and_28_out, Acertado01, and_29_out);
  and and_29 (and_29_out, ~Linha_N2[0], ~Linha_N2[1], Coluna_N2[0], ~Coluna_N2[1], Estado_2);  // AND_Gate
  and and_30 (and_30_out, Linha_N1[0], ~Linha_N1[1], Coluna_N1[0], ~Coluna_N1[1], ~Estado_0);  // AND_Gate
  or or_7 (Mux11, and_30_out, Acertado11, and_31_out);
  and and_31 (and_31_out, Linha_N2[0], ~Linha_N2[1], Coluna_N2[0], ~Coluna_N2[1], Estado_2);  // AND_Gate
  and and_32 (and_32_out, ~Linha_N1[0], Linha_N1[1], Coluna_N1[0], ~Coluna_N1[1], ~Estado_0);  // AND_Gate
  or or_8 (Mux21, and_32_out, Acertado21, and_33_out);
  and and_33 (and_33_out, ~Linha_N2[0], Linha_N2[1], Coluna_N2[0], ~Coluna_N2[1], Estado_2);  // AND_Gate
  and and_34 (and_34_out, Linha_N1[0], Linha_N1[1], Coluna_N1[0], ~Coluna_N1[1], ~Estado_0);  // AND_Gate
  or or_9 (Mux31, and_34_out, Acertado31, and_35_out);
  and and_35 (and_35_out, Linha_N2[0], Linha_N2[1], Coluna_N2[0], ~Coluna_N2[1], Estado_2);  // AND_Gate
  not not_1 (Jogador_1, Jogador_2);
  Counter #(.width(2), .max('h3)) counter_5 (.Q(nColuna), .clk(Coluna), .clr(Reset));  // open: load, D, count, carry
  and and_36 (and_36_out, Confirma, ~Bloqueado);  // AND_Gate
  and and_37 (and_37_out, ~Linha_N1[0], ~Linha_N1[1], ~Coluna_N1[0], Coluna_N1[1], ~Estado_0);  // AND_Gate
  and and_38 (and_38_out, ~Linha_N2[0], ~Linha_N2[1], ~Coluna_N2[0], Coluna_N2[1], Estado_2);  // AND_Gate
  and and_39 (and_39_out, Linha_N1[0], ~Linha_N1[1], ~Coluna_N1[0], Coluna_N1[1], ~Estado_0);  // AND_Gate
  and and_40 (and_40_out, Linha_N2[0], ~Linha_N2[1], ~Coluna_N2[0], Coluna_N2[1], Estado_2);  // AND_Gate
  and and_41 (and_41_out, ~Linha_N1[0], Linha_N1[1], ~Coluna_N1[0], Coluna_N1[1], ~Estado_0);  // AND_Gate
  and and_42 (and_42_out, ~Linha_N2[0], Linha_N2[1], ~Coluna_N2[0], Coluna_N2[1], Estado_2);  // AND_Gate
  and and_43 (and_43_out, Linha_N1[0], Linha_N1[1], ~Coluna_N1[0], Coluna_N1[1], ~Estado_0);  // AND_Gate
  and and_44 (and_44_out, Linha_N2[0], Linha_N2[1], ~Coluna_N2[0], Coluna_N2[1], Estado_2);  // AND_Gate
  Counter #(.width(2), .max('h3)) counter_6 (
    .Q(counter_6_q), .clk(and_36_out), .clr(or_10_out));  // open: load, D, count, carry
  or or_10 (or_10_out, Estado_3, Reset);
  or or_11 (Mux02, and_37_out, Acertado02, and_38_out);
  or or_12 (Mux12, and_39_out, Acertado12, and_40_out);
  or or_13 (Mux22, and_41_out, Acertado22, and_42_out);
  or or_14 (Mux32, and_43_out, Acertado32, and_44_out);
  Comparator #(.width(4), .mode("unsigned")) comparator_2 (
    .a({Coluna_N1, Linha_N1}), .b({nColuna, nLinha}), .eq(comparator_2_eq));  // open: gt, lt
  Register #(.width(2)) register_1 (.D(nColuna), .Q(Coluna_N1), .clk(and_45_out), .clr(Reset));  // open: en
  Register #(.width(2)) register_2 (.D(nLinha), .Q(Linha_N1), .clk(and_45_out), .clr(Reset));  // open: en
  and and_45 (and_45_out, Confirma, Estado_0);
  and and_46 (Estado_0, ~counter_6_q[0], ~counter_6_q[1]);  // AND_Gate
  and and_47 (Estado_1, counter_6_q[0], ~counter_6_q[1]);  // AND_Gate
  and and_48 (Estado_2, ~counter_6_q[0], counter_6_q[1]);  // AND_Gate
  and and_49 (Estado_3, counter_6_q[0], counter_6_q[1]);
  and and_50 (V2, Estado_1, comparator_2_eq);
  and and_51 (and_51_out, ~Linha_N1[0], ~Linha_N1[1], Coluna_N1[0], Coluna_N1[1], ~Estado_0);  // AND_Gate
  and and_52 (and_52_out, ~Linha_N2[0], ~Linha_N2[1], Coluna_N2[0], Coluna_N2[1], Estado_2);  // AND_Gate
  and and_53 (and_53_out, Linha_N1[0], ~Linha_N1[1], Coluna_N1[0], Coluna_N1[1], ~Estado_0);  // AND_Gate
  and and_54 (and_54_out, Linha_N2[0], ~Linha_N2[1], Coluna_N2[0], Coluna_N2[1], Estado_2);  // AND_Gate
  and and_55 (and_55_out, ~Linha_N1[0], Linha_N1[1], Coluna_N1[0], Coluna_N1[1], ~Estado_0);  // AND_Gate
  and and_56 (and_56_out, ~Linha_N2[0], Linha_N2[1], Coluna_N2[0], Coluna_N2[1], Estado_2);  // AND_Gate
  and and_57 (and_57_out, Linha_N1[0], Linha_N1[1], Coluna_N1[0], Coluna_N1[1], ~Estado_0);  // AND_Gate
  and and_58 (and_58_out, Linha_N2[0], Linha_N2[1], Coluna_N2[0], Coluna_N2[1], Estado_2);
  and and_59 (and_59_out, Confirma, Estado_1);
  or or_15 (Mux03, and_51_out, Acertado03, and_52_out);
  or or_16 (Mux13, and_53_out, Acertado13, and_54_out);
  or or_17 (Mux23, and_55_out, Acertado23, and_56_out);
  or or_18 (Mux33, and_57_out, Acertado33, and_58_out);
  Register #(.width(2)) register_3 (.D(nColuna), .Q(Coluna_N2), .clk(and_59_out), .clr(Reset));  // open: en
  Register #(.width(2)) register_4 (.D(nLinha), .Q(Linha_N2), .clk(and_59_out), .clr(Reset));  // open: en
  and and_60 (and_60_out, Verifica, ~Linha_N1[0], ~Linha_N1[1], ~Coluna_N1[0], ~Coluna_N1[1]);  // AND_Gate
  and and_61 (and_61_out, Verifica, ~Linha_N2[0], ~Linha_N2[1], ~Coluna_N2[0], ~Coluna_N2[1]);  // AND_Gate
  and and_62 (and_62_out, Verifica, ~Linha_N1[0], ~Linha_N1[1], Coluna_N1[0], ~Coluna_N1[1]);  // AND_Gate
  and and_63 (and_63_out, Verifica, ~Linha_N2[0], ~Linha_N2[1], Coluna_N2[0], ~Coluna_N2[1]);  // AND_Gate
  and and_64 (and_64_out, Verifica, ~Linha_N1[0], ~Linha_N1[1], ~Coluna_N1[0], Coluna_N1[1]);  // AND_Gate
  and and_65 (and_65_out, Verifica, ~Linha_N2[0], ~Linha_N2[1], ~Coluna_N2[0], Coluna_N2[1]);  // AND_Gate
  and and_66 (and_66_out, Verifica, ~Linha_N1[0], ~Linha_N1[1], Coluna_N1[0], Coluna_N1[1]);  // AND_Gate
  and and_67 (and_67_out, Verifica, ~Linha_N2[0], ~Linha_N2[1], Coluna_N2[0], Coluna_N2[1]);  // AND_Gate
  and and_68 (and_68_out, Verifica, Linha_N1[0], ~Linha_N1[1], ~Coluna_N1[0], ~Coluna_N1[1]);  // AND_Gate
  and and_69 (and_69_out, Verifica, Linha_N2[0], ~Linha_N2[1], ~Coluna_N2[0], ~Coluna_N2[1]);  // AND_Gate
  and and_70 (and_70_out, Verifica, Linha_N1[0], ~Linha_N1[1], Coluna_N1[0], ~Coluna_N1[1]);  // AND_Gate
  and and_71 (and_71_out, Verifica, Linha_N2[0], ~Linha_N2[1], Coluna_N2[0], ~Coluna_N2[1]);  // AND_Gate
  and and_72 (and_72_out, Verifica, Linha_N1[0], ~Linha_N1[1], ~Coluna_N1[0], Coluna_N1[1]);  // AND_Gate
  and and_73 (and_73_out, Verifica, Linha_N2[0], ~Linha_N2[1], ~Coluna_N2[0], Coluna_N2[1]);  // AND_Gate
  and and_74 (and_74_out, Verifica, Linha_N1[0], ~Linha_N1[1], Coluna_N1[0], Coluna_N1[1]);  // AND_Gate
  and and_75 (and_75_out, Verifica, Linha_N2[0], ~Linha_N2[1], Coluna_N2[0], Coluna_N2[1]);  // AND_Gate
  and and_76 (and_76_out, Verifica, ~Linha_N1[0], Linha_N1[1], ~Coluna_N1[0], ~Coluna_N1[1]);  // AND_Gate
  and and_77 (and_77_out, Verifica, ~Linha_N2[0], Linha_N2[1], ~Coluna_N2[0], ~Coluna_N2[1]);  // AND_Gate
  and and_78 (and_78_out, Verifica, ~Linha_N1[0], Linha_N1[1], Coluna_N1[0], ~Coluna_N1[1]);  // AND_Gate
  and and_79 (and_79_out, Verifica, ~Linha_N2[0], Linha_N2[1], Coluna_N2[0], ~Coluna_N2[1]);  // AND_Gate
  and and_80 (and_80_out, Verifica, ~Linha_N1[0], Linha_N1[1], ~Coluna_N1[0], Coluna_N1[1]);  // AND_Gate
  and and_81 (and_81_out, Verifica, ~Linha_N2[0], Linha_N2[1], ~Coluna_N2[0], Coluna_N2[1]);  // AND_Gate
  and and_82 (and_82_out, Verifica, ~Linha_N1[0], Linha_N1[1], Coluna_N1[0], Coluna_N1[1]);  // AND_Gate
  and and_83 (and_83_out, Verifica, ~Linha_N2[0], Linha_N2[1], Coluna_N2[0], Coluna_N2[1]);  // AND_Gate
  and and_84 (and_84_out, Verifica, Linha_N1[0], Linha_N1[1], ~Coluna_N1[0], ~Coluna_N1[1]);  // AND_Gate
  and and_85 (and_85_out, Verifica, Linha_N2[0], Linha_N2[1], ~Coluna_N2[0], ~Coluna_N2[1]);  // AND_Gate
  and and_86 (and_86_out, Verifica, Linha_N1[0], Linha_N1[1], Coluna_N1[0], ~Coluna_N1[1]);  // AND_Gate
  and and_87 (and_87_out, Verifica, Linha_N2[0], Linha_N2[1], Coluna_N2[0], ~Coluna_N2[1]);  // AND_Gate
  and and_88 (and_88_out, Verifica, Linha_N1[0], Linha_N1[1], ~Coluna_N1[0], Coluna_N1[1]);  // AND_Gate
  and and_89 (and_89_out, Verifica, Linha_N2[0], Linha_N2[1], ~Coluna_N2[0], Coluna_N2[1]);  // AND_Gate
  and and_90 (and_90_out, Verifica, Linha_N1[0], Linha_N1[1], Coluna_N1[0], Coluna_N1[1]);
  and and_91 (and_91_out, Verifica, Linha_N2[0], Linha_N2[1], Coluna_N2[0], Coluna_N2[1]);
  D_Flip_Flop d_ff_1 (.Q(Acertado00), .preset(or_19_out), .reset(Reset));  // open: clk, D, Qn, en
  or or_19 (or_19_out, and_60_out, and_61_out);
  D_Flip_Flop d_ff_2 (.Q(Acertado01), .preset(or_20_out), .reset(Reset));  // open: clk, D, Qn, en
  or or_20 (or_20_out, and_62_out, and_63_out);
  D_Flip_Flop d_ff_3 (.Q(Acertado02), .preset(or_21_out), .reset(Reset));  // open: clk, D, Qn, en
  or or_21 (or_21_out, and_64_out, and_65_out);
  D_Flip_Flop d_ff_4 (.Q(Acertado03), .preset(or_22_out), .reset(Reset));  // open: clk, D, Qn, en
  or or_22 (or_22_out, and_66_out, and_67_out);
  D_Flip_Flop d_ff_5 (.Q(Acertado10), .preset(or_23_out), .reset(Reset));  // open: clk, D, Qn, en
  or or_23 (or_23_out, and_68_out, and_69_out);
  D_Flip_Flop d_ff_6 (.Q(Acertado11), .preset(or_24_out), .reset(Reset));  // open: clk, D, Qn, en
  or or_24 (or_24_out, and_70_out, and_71_out);
  D_Flip_Flop d_ff_7 (.Q(Acertado12), .preset(or_25_out), .reset(Reset));  // open: clk, D, Qn, en
  or or_25 (or_25_out, and_72_out, and_73_out);
  D_Flip_Flop d_ff_8 (.Q(Acertado13), .preset(or_26_out), .reset(Reset));  // open: clk, D, Qn, en
  or or_26 (or_26_out, and_74_out, and_75_out);
  D_Flip_Flop d_ff_9 (.Q(Acertado20), .preset(or_27_out), .reset(Reset));  // open: clk, D, Qn, en
  or or_27 (or_27_out, and_76_out, and_77_out);
  D_Flip_Flop d_ff_10 (.Q(Acertado21), .preset(or_28_out), .reset(Reset));  // open: clk, D, Qn, en
  or or_28 (or_28_out, and_78_out, and_79_out);
  D_Flip_Flop d_ff_11 (.Q(Acertado22), .preset(or_29_out), .reset(Reset));  // open: clk, D, Qn, en
  or or_29 (or_29_out, and_80_out, and_81_out);
  D_Flip_Flop d_ff_12 (.Q(Acertado23), .preset(or_30_out), .reset(Reset));  // open: clk, D, Qn, en
  or or_30 (or_30_out, and_82_out, and_83_out);
  D_Flip_Flop d_ff_13 (.Q(Acertado30), .preset(or_31_out), .reset(Reset));  // open: clk, D, Qn, en
  or or_31 (or_31_out, and_84_out, and_85_out);
  D_Flip_Flop d_ff_14 (.Q(Acertado31), .preset(or_32_out), .reset(Reset));  // open: clk, D, Qn, en
  or or_32 (or_32_out, and_86_out, and_87_out);
  D_Flip_Flop d_ff_15 (.Q(Acertado32), .preset(or_33_out), .reset(Reset));  // open: clk, D, Qn, en
  or or_33 (or_33_out, and_88_out, and_89_out);
  D_Flip_Flop d_ff_16 (.Q(Acertado33), .preset(or_34_out), .reset(Reset));  // open: clk, D, Qn, en
  or or_34 (or_34_out, and_90_out, and_91_out);
  and and_92 (and_92_out, L00, Acertado00);
  and and_93 (and_93_out, L01, Acertado01);
  and and_94 (and_94_out, L02, Acertado02);
  and and_95 (and_95_out, L03, Acertado03);
  and and_96 (and_96_out, L10, Acertado10);
  and and_97 (and_97_out, L11, Acertado11);
  and and_98 (and_98_out, L12, Acertado12);
  and and_99 (and_99_out, L13, Acertado13);
  and and_100 (and_100_out, L20, Acertado20);
  and and_101 (and_101_out, L21, Acertado21);
  and and_102 (and_102_out, L22, Acertado22);
  and and_103 (and_103_out, L23, Acertado23);
  and and_104 (and_104_out, L30, Acertado30);
  and and_105 (and_105_out, L31, Acertado31);
  and and_106 (and_106_out, L32, Acertado32);
  and and_107 (and_107_out, L33, Acertado33);
  or or_35 (V1, and_92_out, and_93_out, and_94_out, and_95_out, and_96_out, and_97_out, and_98_out, and_99_out, and_100_out, and_101_out, and_102_out, and_103_out, and_104_out, and_105_out, and_106_out, and_107_out);

  // Notes on the sheet:
  //   Linha
  //   Coluna
  //   Confirma
endmodule
